# Fritzing sketch TeaBot (saved by Fritzing 1.0.2b)

parts:
  Arduino_Nano = Arduino Nano (Rev3.0)
  Servo = Basic Servo
  OLED = OLED Monochrome 128x32 I2C [part_number=931]
  USB_C_PWR_in = Adafruit USB Type C Breakout [part_number=4090]
  RotEncoder = KY-040 Rotary encoder [package=THT]
  Buzzer = Buzzer 12mm [package=buzzer-12mm-ns]

nets:
  N1: Arduino_Nano.D2, RotEncoder.CLK
  N2: Arduino_Nano.D3, RotEncoder.DT
  N3: Arduino_Nano.D4, RotEncoder.SW
  N4: Arduino_Nano.D9, Servo.pulse
  N5: Arduino_Nano.D10, Buzzer.1
  GND: Arduino_Nano.GND, Servo.gnd, OLED.GND, USB_C_PWR_in.GND, RotEncoder.GND, Buzzer.2
  5V: Arduino_Nano.5V, Servo.vcc, OLED.VIN, USB_C_PWR_in.VBUS, RotEncoder.Vcc
  N6: Arduino_Nano.A5, OLED.SCL
  N7: Arduino_Nano.A4, OLED.SDA
  N8: USB_C_PWR_in.D-, USB_C_PWR_in.D+

custom parts:
  OLED Monochrome 128x32 I2C: These displays are small, only about 1" diagonal, but very readable due to the high contrast of an OLED display. This display is made of 128x32 individual white OLED pixels, each one is turned on or off by the controller chip. Because the display makes its own light, no backlight is required. This reduces the power required to run the OLED and is why the display has such high contrast; we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
  Adafruit USB Type C Breakout: Adafruit breakout board for USB Type C socket.
  KY-040 Rotary encoder: KY-040 Rotary Encoder with switch on breakout borad from AZ Delivery
